// Logisim project Display Hexadecimal.circ as structural Verilog: 2 circuits, main circuit main
module main (
  input  [3:0] A
);

  wire auxiliar_1_d0, auxiliar_1_d1, auxiliar_1_d2, auxiliar_1_d3, auxiliar_1_d4, auxiliar_1_d5,
       auxiliar_1_d6;

  Auxiliar auxiliar_1 (
    .D4(auxiliar_1_d4), .D5(auxiliar_1_d5), .D6(auxiliar_1_d6), .D0(auxiliar_1_d0), .D1(auxiliar_1_d1),
    .D2(auxiliar_1_d2), .D3(auxiliar_1_d3), .A1(A[1]), .A0(A[0]), .A3(A[3]), .A2(A[2]));
  _7_Segment_Display u_7_segment_display_1 (
    .g(auxiliar_1_d6), .f(auxiliar_1_d5), .a(auxiliar_1_d0), .b(auxiliar_1_d1), .e(auxiliar_1_d4),
    .d(auxiliar_1_d3), .c(auxiliar_1_d2));  // open: dp
endmodule

module Auxiliar (
  input  A3,
  input  A2,
  input  A1,
  input  A0,
  output D0,
  output D1,
  output D2,
  output D3,
  output D4,
  output D5,
  output D6
);

  wire and_1_out, and_2_out, and_3_out, and_4_out, and_5_out, and_6_out, and_7_out, and_8_out, and_9_out,
       and_10_out, and_11_out, and_12_out, and_13_out, and_14_out, and_15_out, and_16_out, and_17_out,
       and_18_out, and_19_out, and_20_out, and_21_out, and_22_out, and_23_out, and_24_out, and_25_out,
       and_26_out, and_27_out, and_28_out, and_29_out, and_30_out, and_31_out, and_32_out, and_33_out,
       and_34_out, and_35_out;

  and and_1 (and_1_out, A1, ~A3);  // AND_Gate
  and and_2 (and_2_out, A1, A2);
  and and_3 (and_3_out, ~A0, ~A2);  // AND_Gate
  and and_4 (and_4_out, ~A1, ~A2, A3);  // AND_Gate
  and and_5 (and_5_out, ~A0, ~A1, A3);  // AND_Gate
  and and_6 (and_6_out, A0, A2, ~A3);  // AND_Gate
  and and_7 (and_7_out, ~A2, ~A3);  // AND_Gate
  and and_8 (and_8_out, ~A0, ~A2);  // AND_Gate
  and and_9 (and_9_out, A0, ~A1, A3);  // AND_Gate
  and and_10 (and_10_out, A0, A1, ~A3);  // AND_Gate
  and and_11 (and_11_out, ~A0, ~A1, ~A3);  // AND_Gate
  and and_12 (and_12_out, A0, ~A3);  // AND_Gate
  and and_13 (and_13_out, A2, ~A3);  // AND_Gate
  and and_14 (and_14_out, ~A2, A3);  // AND_Gate
  and and_15 (and_15_out, A0, ~A1);  // AND_Gate
  and and_16 (and_16_out, ~A1, ~A3);  // AND_Gate
  and and_17 (and_17_out, ~A1, A3);  // AND_Gate
  and and_18 (and_18_out, A0, A1, ~A2);  // AND_Gate
  and and_19 (and_19_out, ~A0, A1, A2);  // AND_Gate
  and and_20 (and_20_out, ~A0, ~A2, ~A3);  // AND_Gate
  and and_21 (and_21_out, A0, ~A1, A2);  // AND_Gate
  and and_22 (and_22_out, ~A0, A1);  // AND_Gate
  and and_23 (and_23_out, ~A0, ~A2);  // AND_Gate
  and and_24 (and_24_out, A2, A3);
  and and_25 (and_25_out, A0, A1, A3);
  and and_26 (and_26_out, ~A0, ~A1);  // AND_Gate
  and and_27 (and_27_out, ~A2, A3);  // AND_Gate
  and and_28 (and_28_out, A1, A3);
  and and_29 (and_29_out, ~A0, A2);  // AND_Gate
  and and_30 (and_30_out, ~A1, A2, ~A3);  // AND_Gate
  and and_31 (and_31_out, ~A2, A3);  // AND_Gate
  and and_32 (and_32_out, ~A0, A1);  // AND_Gate
  and and_33 (and_33_out, A0, A3);
  and and_34 (and_34_out, A1, ~A2);  // AND_Gate
  and and_35 (and_35_out, ~A1, A2, ~A3);  // AND_Gate
  or or_1 (D0, and_1_out, and_2_out, and_3_out, and_4_out, and_5_out, and_6_out);
  or or_2 (D1, and_7_out, and_8_out, and_9_out, and_10_out, and_11_out);
  or or_3 (D2, and_12_out, and_13_out, and_14_out, and_15_out, and_16_out);
  or or_4 (D3, and_17_out, and_18_out, and_19_out, and_20_out, and_21_out);
  or or_5 (D4, and_22_out, and_23_out, and_24_out, and_25_out);
  or or_6 (D5, and_26_out, and_27_out, and_28_out, and_29_out, and_30_out);
  or or_7 (D6, and_31_out, and_32_out, and_33_out, and_34_out, and_35_out);
endmodule
