// Logisim project FullAdder.circ as structural Verilog: 2 circuits, main circuit main
module main (
  input  A0,
  input  A1,
  input  A2,
  input  A3,
  input  B0,
  input  B1,
  input  B2,
  input  B3,
  output CoutFinal,
  output [3:0] S
);

  wire somador_1_cout, somador_2_cout, somador_3_cout;

  Somador somador_1 (.S(S[0]), .Cout(somador_1_cout), .B(B0), .Cin(1'b0), .A(A0));
  Somador somador_2 (.S(S[1]), .Cout(somador_2_cout), .B(B1), .Cin(somador_1_cout), .A(A1));
  Somador somador_3 (.S(S[2]), .Cout(somador_3_cout), .B(B2), .Cin(somador_2_cout), .A(A2));
  Somador somador_4 (.S(S[3]), .Cout(CoutFinal), .B(B3), .Cin(somador_3_cout), .A(A3));
endmodule

module Somador (
  input  A,
  input  B,
  input  Cin,
  output Cout,
  output S
);

  wire and_1_out, and_2_out, and_3_out, xor_1_out;

  xor xor_1 (xor_1_out, A, B);
  and and_1 (and_1_out, A, B);
  and and_2 (and_2_out, A, Cin);
  and and_3 (and_3_out, B, Cin);
  xor xor_2 (S, xor_1_out, Cin);
  or or_1 (Cout, and_1_out, and_2_out, and_3_out);
endmodule
