// Logisim project Somador_e_subtrator.circ as structural Verilog: 2 circuits, main circuit main
module main (
  input  [3:0] A,
  input  OP,
  input  [3:0] B,
  output CoutFinal,
  output [3:0] S
);

  wire somador_1_carryout, somador_2_carryout, somador_3_carryout;
  wire [3:0] multiplexer_1_out, not_1_out;

  Multiplexer #(.width(4)) multiplexer_1 (.in0(B), .in1(not_1_out), .out(multiplexer_1_out), .sel(OP));
  assign not_1_out = ~B;  // NOT_Gate not_1, 4 bits wide
  Somador somador_1 (.Soma(S[0]), .CarryOut(somador_1_carryout), .CarryIn(OP), .A(A[0]), .B(multiplexer_1_out[0]));
  Somador somador_2 (
    .Soma(S[1]), .CarryOut(somador_2_carryout), .CarryIn(somador_1_carryout), .A(A[1]),
    .B(multiplexer_1_out[1]));
  Somador somador_3 (
    .Soma(S[2]), .CarryOut(somador_3_carryout), .CarryIn(somador_2_carryout), .A(A[2]),
    .B(multiplexer_1_out[2]));
  Somador somador_4 (
    .Soma(S[3]), .CarryOut(CoutFinal), .CarryIn(somador_3_carryout), .A(A[3]), .B(multiplexer_1_out[3]));

  // Notes on the sheet:
  //   OP = 0 ---> Soma
  //   OP = 1 ---> Subtração ( Caso A < B, será feito em complemento de 2)
endmodule

module Somador (
  input  A,
  input  B,
  input  CarryIn,
  output CarryOut,
  output Soma
);

  wire and_1_out, and_2_out, and_3_out, xor_1_out;

  xor xor_1 (xor_1_out, A, B);
  and and_1 (and_1_out, A, B);
  and and_2 (and_2_out, A, CarryIn);
  and and_3 (and_3_out, B, CarryIn);
  xor xor_2 (Soma, xor_1_out, CarryIn);
  or or_1 (CarryOut, and_1_out, and_2_out, and_3_out);
endmodule
