// Logisim project ContadorGray.circ as structural Verilog: 5 circuits, main circuit Circuito
module Circuito (
  output [3:0] out_1
);

  wire clock_1_out, q0_1_j0, q0_1_k0, q1_1_j1, q1_1_k1, q2_1_j2, q2_1_k2, q3_1_j3, q3_1_k3;

  Clock clock_1 (.out(clock_1_out));
  Q0 q0_1 (.K0(q0_1_k0), .J0(q0_1_j0), .Q3(out_1[3]), .Q2(out_1[2]), .Q1(out_1[1]));
  J_K_Flip_Flop j_k_ff_1 (.J(q0_1_j0), .K(q0_1_k0), .clk(clock_1_out), .Q(out_1[0]));  // open: Qn, preset, reset
  Q1 q1_1 (.J1(q1_1_j1), .K1(q1_1_k1), .Q3(out_1[3]), .Q2(out_1[2]), .Q0(out_1[0]));
  J_K_Flip_Flop j_k_ff_2 (.J(q1_1_j1), .K(q1_1_k1), .clk(clock_1_out), .Q(out_1[1]));  // open: Qn, preset, reset
  Q2 q2_1 (.J2(q2_1_j2), .K2(q2_1_k2), .Q1(out_1[1]), .Q0(out_1[0]), .Q3(out_1[3]));
  J_K_Flip_Flop j_k_ff_3 (.J(q2_1_j2), .K(q2_1_k2), .clk(clock_1_out), .Q(out_1[2]));  // open: Qn, preset, reset
  Q3 q3_1 (.J3(q3_1_j3), .K3(q3_1_k3), .Q2(out_1[2]), .Q1(out_1[1]), .Q0(out_1[0]));
  J_K_Flip_Flop j_k_ff_4 (.J(q3_1_j3), .K(q3_1_k3), .clk(clock_1_out), .Q(out_1[3]));  // open: Qn, preset, reset
  Hex_Digit_Display hex_digit_display_1 (.value(out_1));  // open: dp
endmodule

module Q3 (
  input  Q2,
  input  Q1,
  input  Q0,
  output J3,
  output K3
);

  and and_1 (J3, ~Q0, ~Q1, Q2);  // AND_Gate
  and and_2 (K3, ~Q0, ~Q1, ~Q2);  // AND_Gate
endmodule

module Q2 (
  input  Q3,
  input  Q1,
  input  Q0,
  output J2,
  output K2
);

  and and_1 (J2, ~Q0, Q1, ~Q3);  // AND_Gate
  and and_2 (K2, ~Q0, Q1, Q3);  // AND_Gate
endmodule

module Q1 (
  input  Q3,
  input  Q2,
  input  Q0,
  output J1,
  output K1
);

  wire and_1_out, and_2_out, and_3_out, and_4_out;

  and and_1 (and_1_out, Q0, ~Q2, ~Q3);  // AND_Gate
  and and_2 (and_2_out, Q0, Q2, Q3);
  and and_3 (and_3_out, Q0, Q2, ~Q3);  // AND_Gate
  and and_4 (and_4_out, Q0, ~Q2, Q3);  // AND_Gate
  or or_1 (J1, and_1_out, and_2_out);
  or or_2 (K1, and_3_out, and_4_out);
endmodule

module Q0 (
  input  Q3,
  input  Q2,
  input  Q1,
  output J0,
  output K0
);

  wire and_1_out, and_2_out, and_3_out, and_4_out, and_5_out, and_6_out, and_7_out, and_8_out;

  and and_1 (and_1_out, ~Q1, ~Q2, ~Q3);  // AND_Gate
  and and_2 (and_2_out, ~Q1, Q2, Q3);  // AND_Gate
  and and_3 (and_3_out, Q1, ~Q2, Q3);  // AND_Gate
  and and_4 (and_4_out, Q1, Q2, ~Q3);  // AND_Gate
  and and_5 (and_5_out, Q1, Q2, Q3);
  and and_6 (and_6_out, ~Q1, ~Q2, Q3);  // AND_Gate
  and and_7 (and_7_out, ~Q1, Q2, ~Q3);  // AND_Gate
  and and_8 (and_8_out, Q1, ~Q2, ~Q3);  // AND_Gate
  or or_1 (J0, and_1_out, and_2_out, and_3_out, and_4_out);
  or or_2 (K0, and_5_out, and_6_out, and_7_out, and_8_out);
endmodule
