// Logisim project Cronômetro.circ as structural Verilog: 3 circuits, main circuit main
module main (
  input  ENABLE
);

  wire and_1_out, clock_1_out, cronometro_0a5_2_cout, cronometro_1_cout, cronometro_2_cout, RESET_out;
  wire [3:0] cronometro_0a5_1_contador0a5, cronometro_0a5_2_contador0a5, cronometro_1_contador0a9,
       cronometro_2_contador0a9;

  Hex_Digit_Display hex_digit_display_1 (.value(cronometro_0a5_1_contador0a5));  // open: dp
  CRONOMETRO_0A5 cronometro_0a5_1 (
    .Contador0A5(cronometro_0a5_1_contador0a5), .RESET(RESET_out), .in_1(cronometro_1_cout));  // open: COUT
  Hex_Digit_Display hex_digit_display_2 (.value(cronometro_1_contador0a9));  // open: dp
  CRONOMETRO cronometro_1 (
    .COUT(cronometro_1_cout), .Contador0A9(cronometro_1_contador0a9), .RESET(RESET_out),
    .in_1(cronometro_0a5_2_cout));
  Hex_Digit_Display hex_digit_display_3 (.value(cronometro_0a5_2_contador0a5));  // open: dp
  CRONOMETRO_0A5 cronometro_0a5_2 (
    .COUT(cronometro_0a5_2_cout), .Contador0A5(cronometro_0a5_2_contador0a5), .RESET(RESET_out),
    .in_1(cronometro_2_cout));
  Hex_Digit_Display hex_digit_display_4 (.value(cronometro_2_contador0a9));  // open: dp
  CRONOMETRO cronometro_2 (
    .COUT(cronometro_2_cout), .Contador0A9(cronometro_2_contador0a9), .RESET(RESET_out), .in_1(and_1_out));
  and and_1 (and_1_out, ENABLE, clock_1_out);
  Clock clock_1 (.out(clock_1_out));
  Button RESET (.out(RESET_out));
endmodule

module CRONOMETRO (
  input  in_1,
  input  RESET,
  output [3:0] Contador0A9,
  output COUT
);

  wire and_1_out, or_1_out;

  T_Flip_Flop #(.trigger("falling")) t_ff_1 (
    .T(1'b1), .clk(in_1), .Q(Contador0A9[0]), .reset(or_1_out));  // open: Qn, preset
  T_Flip_Flop #(.trigger("falling")) t_ff_2 (
    .T(1'b1), .clk(Contador0A9[0]), .Q(Contador0A9[1]), .reset(or_1_out));  // open: Qn, preset
  T_Flip_Flop #(.trigger("falling")) t_ff_3 (
    .T(1'b1), .clk(Contador0A9[1]), .Q(Contador0A9[2]), .reset(or_1_out));  // open: Qn, preset
  T_Flip_Flop #(.trigger("falling")) t_ff_4 (
    .T(1'b1), .clk(Contador0A9[2]), .Q(Contador0A9[3]), .reset(or_1_out));  // open: Qn, preset
  or or_1 (or_1_out, and_1_out, RESET);
  and and_1 (and_1_out, Contador0A9[1], Contador0A9[3]);
  Hex_Digit_Display hex_digit_display_1 (.value(Contador0A9));  // open: dp

  assign COUT = Contador0A9[3];
endmodule

module CRONOMETRO_0A5 (
  input  in_1,
  input  RESET,
  output [3:0] Contador0A5,
  output COUT
);

  wire and_1_out, or_1_out;

  T_Flip_Flop #(.trigger("falling")) t_ff_1 (
    .T(1'b1), .clk(in_1), .Q(Contador0A5[0]), .reset(or_1_out));  // open: Qn, preset
  T_Flip_Flop #(.trigger("falling")) t_ff_2 (
    .T(1'b1), .clk(Contador0A5[0]), .Q(Contador0A5[1]), .reset(or_1_out));  // open: Qn, preset
  T_Flip_Flop #(.trigger("falling")) t_ff_3 (
    .T(1'b1), .clk(Contador0A5[1]), .Q(Contador0A5[2]), .reset(or_1_out));  // open: Qn, preset
  or or_1 (or_1_out, and_1_out, RESET);
  and and_1 (and_1_out, Contador0A5[1], Contador0A5[2]);
  Hex_Digit_Display hex_digit_display_1 (.value({1'b0, Contador0A5[2:0]}));  // open: dp

  assign Contador0A5[3] = 1'b0;
  assign COUT = Contador0A5[2];
endmodule
