// Logisim project Porta com Tranca.circ as structural Verilog: 4 circuits, main circuit main
module main (
);

  wire button_1_out, button_2_out, button_3_out, button_4_out, button_5_out, button_6_out, button_7_out,
       button_8_out, button_9_out, button_10_out, button_11_out, senha_1_abre, senha_1_erro;

  Button button_1 (.out(button_1_out));
  Button button_2 (.out(button_2_out));
  Button button_3 (.out(button_3_out));
  Button button_4 (.out(button_4_out));
  Button button_5 (.out(button_5_out));
  Button button_6 (.out(button_6_out));
  Button button_7 (.out(button_7_out));
  Button button_8 (.out(button_8_out));
  Button button_9 (.out(button_9_out));
  Button button_10 (.out(button_10_out));
  Button button_11 (.out(button_11_out));
  Senha senha_1 (
    .Enter(button_1_out), .a1(button_2_out), .a2(button_3_out), .a3(button_4_out), .a4(button_5_out),
    .a5(button_6_out), .a6(button_7_out), .a7(button_8_out), .a8(button_9_out), .a9(button_10_out),
    .RESET(button_11_out), .ABRE(senha_1_abre), .ERRO(senha_1_erro));
  LED led_1 (.in(senha_1_abre));
  LED led_2 (.in(senha_1_erro));
endmodule

module teclado (
  input  enter,
  input  in_2,
  input  in_3,
  input  in_4,
  input  in_5,
  input  in_6,
  input  in_7,
  input  in_8,
  input  in_9,
  input  in_10,
  output A3,
  output A2,
  output A1,
  output A0,
  output IMPUT
);

  or or_1 (A3, in_9, in_10);
  or or_2 (A2, in_5, in_6, in_7, in_8);
  or or_3 (A1, in_3, in_4, in_7, in_8);
  or or_4 (A0, in_2, in_4, in_6, in_8, in_10);
  or or_5 (IMPUT, in_10, in_9, in_8, in_7, in_6, in_5, in_4, in_3, in_2, enter);

  // Notes on the sheet:
  //     1   2   3    4   5   6   7   8   9   
endmodule

module Senha (
  input  Enter,
  input  a1,
  input  a2,
  input  a3,
  input  a4,
  input  a5,
  input  a6,
  input  a7,
  input  a8,
  input  a9,
  input  RESET,
  output ABRE,
  output ERRO
);

  wire and_1_out, and_2_out, and_3_out, and_4_out, and_5_out, and_6_out, and_7_out, comparator_1_eq,
       or_1_out, or_2_out, or_3_out, or_4_out, t_ff_1_q, teclado_1_a0, teclado_1_a1, teclado_1_a2,
       teclado_1_a3, teclado_1_imput, ver_se4_1_out_2, xnor_1_out;
  wire [3:0] d_ff_1_q, Q0_q;

  or or_1 (or_1_out, Q0_q[2], xnor_1_out);
  teclado teclado_1 (
    .A3(teclado_1_a3), .A2(teclado_1_a2), .A1(teclado_1_a1), .A0(teclado_1_a0), .IMPUT(teclado_1_imput),
    .enter(Enter), .in_2(a1), .in_3(a2), .in_4(a3), .in_5(a4), .in_6(a5), .in_7(a6), .in_8(a7), .in_9(a8),
    .in_10(a9));
  xnor xnor_1 (xnor_1_out, Q0_q[1], Q0_q[3]);
  and and_1 (and_1_out, ~Q0_q[1], ~Q0_q[2], ~Q0_q[3]);  // AND_Gate
  J_K_Flip_Flop Q0 (
    .J(and_1_out), .K(or_1_out), .clk(teclado_1_imput), .Q(Q0_q[0]), .reset(or_4_out));  // open: Qn, preset
  D_Flip_Flop d_ff_1 (.D(teclado_1_a0), .clk(teclado_1_imput), .Q(d_ff_1_q[0]), .reset(or_4_out));  // open: Qn, preset
  or or_2 (or_2_out, ~Q0_q[0], Q0_q[2], Q0_q[3]);  // OR_Gate
  and and_2 (and_2_out, Q0_q[0], ~Q0_q[2], Q0_q[3]);  // AND_Gate
  J_K_Flip_Flop Q1 (
    .J(and_2_out), .K(or_2_out), .clk(teclado_1_imput), .Q(Q0_q[1]), .reset(or_4_out));  // open: Qn, preset
  D_Flip_Flop d_ff_2 (.D(teclado_1_a1), .clk(teclado_1_imput), .Q(d_ff_1_q[1]), .reset(or_4_out));  // open: Qn, preset
  D_Flip_Flop d_ff_3 (.D(teclado_1_a2), .clk(teclado_1_imput), .Q(d_ff_1_q[2]), .reset(or_4_out));  // open: Qn, preset
  or or_3 (or_3_out, ~Q0_q[0], ~Q0_q[1], Q0_q[3]);  // OR_Gate
  and and_3 (and_3_out, Q0_q[0], Q0_q[1], ~Q0_q[3]);  // AND_Gate
  J_K_Flip_Flop Q2 (
    .J(and_3_out), .K(or_3_out), .clk(teclado_1_imput), .Q(Q0_q[2]), .reset(or_4_out));  // open: Qn, preset
  D_Flip_Flop d_ff_4 (.D(teclado_1_a3), .clk(teclado_1_imput), .Q(d_ff_1_q[3]), .reset(or_4_out));  // open: Qn, preset
  and and_4 (and_4_out, ~Q0_q[0], ~Q0_q[1], ~Q0_q[2]);  // AND_Gate
  J_K_Flip_Flop Q3 (.J(and_4_out), .K(1'b1), .clk(teclado_1_imput), .Q(Q0_q[3]), .reset(or_4_out));  // open: Qn, preset
  or or_4 (or_4_out, and_5_out, Enter, RESET);
  ver_se4 ver_se4_1 (.out_2(ver_se4_1_out_2), .in_1(Q0_q));
  and and_5 (and_5_out, teclado_1_imput, ~comparator_1_eq);  // AND_Gate
  Comparator #(.width(4)) comparator_1 (.a(d_ff_1_q), .b(Q0_q), .eq(comparator_1_eq));  // open: gt, lt
  Hex_Digit_Display hex_digit_display_1 (.value(Q0_q));  // open: dp
  and and_6 (and_6_out, comparator_1_eq, ver_se4_1_out_2);
  T_Flip_Flop t_ff_1 (.T(and_6_out), .clk(and_6_out), .Q(t_ff_1_q), .reset(or_4_out));  // open: Qn, preset
  and and_7 (and_7_out, t_ff_1_q, Enter);
  T_Flip_Flop t_ff_2 (.T(and_7_out), .clk(and_7_out), .Q(ABRE), .reset(RESET));  // open: Qn, preset
  and and_8 (ERRO, ~ABRE, Enter);  // AND_Gate
endmodule

module ver_se4 (
  input  [3:0] in_1,
  output out_2
);

  and and_1 (out_2, ~in_1[0], ~in_1[1], in_1[2], ~in_1[3]);  // AND_Gate
endmodule
