// Logisim project ProjetoDeSemaforo.circ as structural Verilog: 2 circuits, main circuit main
module main (
);

  Semaforo semaforo_1 ();

  // Notes on the sheet:
  //   Projeto de Semáforo
endmodule

module Semaforo (
);

  wire and_1_out, and_2_out, and_3_out, and_4_out, and_5_out, and_6_out, clock_1_out, or_1_out, or_2_out,
       t_ff_1_q, t_ff_2_q, t_ff_3_q, t_ff_4_q;

  T_Flip_Flop #(.trigger("falling")) t_ff_1 (
    .T(1'b1), .clk(clock_1_out), .Q(t_ff_1_q), .reset(and_1_out));  // open: Qn, preset
  Clock clock_1 (.out(clock_1_out));
  T_Flip_Flop #(.trigger("falling")) t_ff_2 (
    .T(1'b1), .clk(t_ff_1_q), .Q(t_ff_2_q), .reset(and_1_out));  // open: Qn, preset
  T_Flip_Flop #(.trigger("falling")) t_ff_3 (
    .T(1'b1), .clk(t_ff_2_q), .Q(t_ff_3_q), .reset(and_1_out));  // open: Qn, preset
  T_Flip_Flop #(.trigger("falling")) t_ff_4 (
    .T(1'b1), .clk(t_ff_3_q), .Q(t_ff_4_q), .reset(and_1_out));  // open: Qn, preset
  and and_1 (and_1_out, t_ff_4_q, t_ff_3_q);
  and and_2 (and_2_out, ~t_ff_3_q, ~t_ff_4_q);  // AND_Gate
  and and_3 (and_3_out, ~t_ff_2_q, ~t_ff_4_q);  // AND_Gate
  and and_4 (and_4_out, t_ff_2_q, t_ff_3_q, ~t_ff_4_q);  // AND_Gate
  and and_5 (and_5_out, ~t_ff_2_q, ~t_ff_3_q, t_ff_4_q);  // AND_Gate
  and and_6 (and_6_out, t_ff_2_q, ~t_ff_3_q, t_ff_4_q);  // AND_Gate
  or or_1 (or_1_out, and_2_out, and_3_out);
  or or_2 (or_2_out, and_4_out, and_5_out);
  LED Pare (.in(or_1_out));
  LED Prossiga (.in(or_2_out));
  LED Atencao (.in(and_6_out));
endmodule
