// Logisim project RelógioCompleto.circ as structural Verilog: 5 circuits, main circuit main
module main (
);

  relogio relogio_1 ();
endmodule

module horas (
  output [3:0] HoraDezena,
  output [3:0] HoraUnidade,
  output Clock
);

  wire and_1_out, and_2_out, and_3_out, minutos_1_clock, or_1_out, or_2_out;
  wire [3:0] minutos_1_minutosdezena, minutos_1_minutosunidade, segundos_1_segundosdezena,
       segundos_1_segundosunidade;

  T_Flip_Flop #(.trigger("falling")) t_ff_1 (
    .T(1'b1), .clk(HoraUnidade[3]), .Q(HoraDezena[0]), .reset(or_1_out));  // open: Qn, preset
  T_Flip_Flop #(.trigger("falling")) t_ff_2 (
    .T(1'b1), .clk(Clock), .Q(HoraUnidade[0]), .reset(or_2_out));  // open: Qn, preset
  minutos minutos_1 (
    .MinutosDezena(minutos_1_minutosdezena), .MinutosUnidade(minutos_1_minutosunidade),
    .Clock(minutos_1_clock), .transmissor(Clock));
  segundos segundos_1 (
    .SegundosDezena(segundos_1_segundosdezena), .SegundosUnidade(segundos_1_segundosunidade),
    .transmissor(minutos_1_clock));
  T_Flip_Flop #(.trigger("falling")) t_ff_3 (
    .T(1'b1), .clk(HoraDezena[0]), .Q(HoraDezena[1]), .reset(or_1_out));  // open: Qn, preset
  T_Flip_Flop #(.trigger("falling")) t_ff_4 (
    .T(1'b1), .clk(HoraUnidade[0]), .Q(HoraUnidade[1]), .reset(or_2_out));  // open: Qn, preset
  T_Flip_Flop #(.trigger("falling")) t_ff_5 (
    .T(1'b1), .clk(HoraUnidade[1]), .Q(HoraUnidade[2]), .reset(or_2_out));  // open: Qn, preset
  T_Flip_Flop #(.trigger("falling")) t_ff_6 (
    .T(1'b1), .clk(HoraUnidade[2]), .Q(HoraUnidade[3]), .reset(or_2_out));  // open: Qn, preset
  or or_1 (or_1_out, and_1_out, and_2_out);
  or or_2 (or_2_out, and_2_out, and_3_out);
  Hex_Digit_Display hex_digit_display_1 (.value({2'b00, HoraDezena[1:0]}));  // open: dp
  Hex_Digit_Display hex_digit_display_2 (.value(HoraUnidade));  // open: dp
  and and_1 (and_1_out, HoraDezena[1], HoraDezena[0]);
  and and_2 (and_2_out, HoraDezena[1], HoraUnidade[2]);
  and and_3 (and_3_out, HoraUnidade[1], HoraUnidade[3]);
  Hex_Digit_Display hex_digit_display_3 (.value(minutos_1_minutosdezena));  // open: dp
  Hex_Digit_Display hex_digit_display_4 (.value(minutos_1_minutosunidade));  // open: dp
  Hex_Digit_Display hex_digit_display_5 (.value(segundos_1_segundosdezena));  // open: dp
  Hex_Digit_Display hex_digit_display_6 (.value(segundos_1_segundosunidade));  // open: dp

  assign HoraDezena[3:2] = 2'b00;
endmodule

module minutos (
  output transmissor,
  output [3:0] MinutosDezena,
  output [3:0] MinutosUnidade,
  output Clock
);

  wire and_1_out, and_2_out;
  wire [3:0] segundos_1_segundosdezena, segundos_1_segundosunidade;

  T_Flip_Flop #(.trigger("falling")) t_ff_1 (
    .T(1'b1), .clk(Clock), .Q(MinutosUnidade[0]), .reset(and_2_out));  // open: Qn, preset
  segundos segundos_1 (
    .SegundosDezena(segundos_1_segundosdezena), .SegundosUnidade(segundos_1_segundosunidade),
    .transmissor(Clock));
  T_Flip_Flop #(.trigger("falling")) t_ff_2 (
    .T(1'b1), .clk(MinutosUnidade[3]), .Q(MinutosDezena[0]), .reset(and_1_out));  // open: Qn, preset
  T_Flip_Flop #(.trigger("falling")) t_ff_3 (
    .T(1'b1), .clk(MinutosUnidade[0]), .Q(MinutosUnidade[1]), .reset(and_2_out));  // open: Qn, preset
  T_Flip_Flop #(.trigger("falling")) t_ff_4 (
    .T(1'b1), .clk(MinutosDezena[0]), .Q(MinutosDezena[1]), .reset(and_1_out));  // open: Qn, preset
  T_Flip_Flop #(.trigger("falling")) t_ff_5 (
    .T(1'b1), .clk(MinutosUnidade[1]), .Q(MinutosUnidade[2]), .reset(and_2_out));  // open: Qn, preset
  T_Flip_Flop #(.trigger("falling")) t_ff_6 (
    .T(1'b1), .clk(MinutosDezena[1]), .Q(MinutosDezena[2]), .reset(and_1_out));  // open: Qn, preset
  T_Flip_Flop #(.trigger("falling")) t_ff_7 (
    .T(1'b1), .clk(MinutosUnidade[2]), .Q(MinutosUnidade[3]), .reset(and_2_out));  // open: Qn, preset
  and and_1 (and_1_out, MinutosDezena[1], MinutosDezena[2]);
  and and_2 (and_2_out, MinutosUnidade[1], MinutosUnidade[3]);
  Hex_Digit_Display hex_digit_display_1 (.value({1'b0, MinutosDezena[2:0]}));  // open: dp
  Hex_Digit_Display hex_digit_display_2 (.value(MinutosUnidade));  // open: dp
  Hex_Digit_Display hex_digit_display_3 (.value(segundos_1_segundosdezena));  // open: dp
  Hex_Digit_Display hex_digit_display_4 (.value(segundos_1_segundosunidade));  // open: dp

  assign MinutosDezena[3] = 1'b0;
  assign transmissor = MinutosDezena[2];
endmodule

module segundos (
  output transmissor,
  output [3:0] SegundosDezena,
  output [3:0] SegundosUnidade
);

  wire and_1_out, and_2_out, clock_1_out;

  Clock clock_1 (.out(clock_1_out));
  T_Flip_Flop #(.trigger("falling")) t_ff_1 (
    .T(1'b1), .clk(SegundosUnidade[3]), .Q(SegundosDezena[0]), .reset(and_1_out));  // open: Qn, preset
  T_Flip_Flop #(.trigger("falling")) t_ff_2 (
    .T(1'b1), .clk(clock_1_out), .Q(SegundosUnidade[0]), .reset(and_2_out));  // open: Qn, preset
  T_Flip_Flop #(.trigger("falling")) t_ff_3 (
    .T(1'b1), .clk(SegundosDezena[0]), .Q(SegundosDezena[1]), .reset(and_1_out));  // open: Qn, preset
  T_Flip_Flop #(.trigger("falling")) t_ff_4 (
    .T(1'b1), .clk(SegundosUnidade[0]), .Q(SegundosUnidade[1]), .reset(and_2_out));  // open: Qn, preset
  T_Flip_Flop #(.trigger("falling")) t_ff_5 (
    .T(1'b1), .clk(SegundosDezena[1]), .Q(SegundosDezena[2]), .reset(and_1_out));  // open: Qn, preset
  T_Flip_Flop #(.trigger("falling")) t_ff_6 (
    .T(1'b1), .clk(SegundosUnidade[1]), .Q(SegundosUnidade[2]), .reset(and_2_out));  // open: Qn, preset
  T_Flip_Flop #(.trigger("falling")) t_ff_7 (
    .T(1'b1), .clk(SegundosUnidade[2]), .Q(SegundosUnidade[3]), .reset(and_2_out));  // open: Qn, preset
  and and_1 (and_1_out, SegundosDezena[1], SegundosDezena[2]);
  and and_2 (and_2_out, SegundosUnidade[1], SegundosUnidade[3]);
  Hex_Digit_Display hex_digit_display_1 (.value({1'b0, SegundosDezena[2:0]}));  // open: dp
  Hex_Digit_Display hex_digit_display_2 (.value(SegundosUnidade));  // open: dp

  assign SegundosDezena[3] = 1'b0;
  assign transmissor = SegundosDezena[2];
endmodule

module relogio (
);

  wire horas_1_clock, minutos_1_clock;
  wire [3:0] horas_1_horadezena, horas_1_horaunidade, minutos_1_minutosdezena, minutos_1_minutosunidade,
       segundos_1_segundosdezena, segundos_1_segundosunidade;

  horas horas_1 (.Clock(horas_1_clock), .HoraDezena(horas_1_horadezena), .HoraUnidade(horas_1_horaunidade));
  minutos minutos_1 (
    .MinutosDezena(minutos_1_minutosdezena), .MinutosUnidade(minutos_1_minutosunidade),
    .Clock(minutos_1_clock), .transmissor(horas_1_clock));
  segundos segundos_1 (
    .SegundosDezena(segundos_1_segundosdezena), .SegundosUnidade(segundos_1_segundosunidade),
    .transmissor(minutos_1_clock));
  Hex_Digit_Display hex_digit_display_1 (.value(horas_1_horadezena));  // open: dp
  Hex_Digit_Display hex_digit_display_2 (.value(horas_1_horaunidade));  // open: dp
  Hex_Digit_Display hex_digit_display_3 (.value(minutos_1_minutosdezena));  // open: dp
  Hex_Digit_Display hex_digit_display_4 (.value(minutos_1_minutosunidade));  // open: dp
  Hex_Digit_Display hex_digit_display_5 (.value(segundos_1_segundosdezena));  // open: dp
  Hex_Digit_Display hex_digit_display_6 (.value(segundos_1_segundosunidade));  // open: dp
endmodule
