// Logisim project relogio.circ as structural Verilog: 2 circuits, main circuit main
module main (
);

  horas horas_1 ();
endmodule

module horas (
);

  wire and_1_out, and_2_out, and_3_out, and_4_out, and_5_out, clock_1_out, or_1_out, or_2_out;
  wire [1:0] t_ff_2_q;
  wire [2:0] t_ff_4_q;
  wire [3:0] t_ff_1_q, t_ff_3_q;

  T_Flip_Flop #(.trigger("falling")) t_ff_1 (
    .T(1'b1), .clk(clock_1_out), .Q(t_ff_1_q[0]), .reset(and_4_out));  // open: Qn, preset
  Clock clock_1 (.out(clock_1_out));
  T_Flip_Flop #(.trigger("falling")) t_ff_2 (
    .T(1'b1), .clk(t_ff_3_q[3]), .Q(t_ff_2_q[0]), .reset(or_1_out));  // open: Qn, preset
  T_Flip_Flop #(.trigger("falling")) t_ff_3 (
    .T(1'b1), .clk(t_ff_4_q[2]), .Q(t_ff_3_q[0]), .reset(or_2_out));  // open: Qn, preset
  T_Flip_Flop #(.trigger("falling")) t_ff_4 (
    .T(1'b1), .clk(t_ff_1_q[3]), .Q(t_ff_4_q[0]), .reset(and_3_out));  // open: Qn, preset
  T_Flip_Flop #(.trigger("falling")) t_ff_5 (
    .T(1'b1), .clk(t_ff_1_q[0]), .Q(t_ff_1_q[1]), .reset(and_4_out));  // open: Qn, preset
  T_Flip_Flop #(.trigger("falling")) t_ff_6 (
    .T(1'b1), .clk(t_ff_2_q[0]), .Q(t_ff_2_q[1]), .reset(or_1_out));  // open: Qn, preset
  T_Flip_Flop #(.trigger("falling")) t_ff_7 (
    .T(1'b1), .clk(t_ff_3_q[0]), .Q(t_ff_3_q[1]), .reset(or_2_out));  // open: Qn, preset
  T_Flip_Flop #(.trigger("falling")) t_ff_8 (
    .T(1'b1), .clk(t_ff_4_q[0]), .Q(t_ff_4_q[1]), .reset(and_3_out));  // open: Qn, preset
  T_Flip_Flop #(.trigger("falling")) t_ff_9 (
    .T(1'b1), .clk(t_ff_1_q[1]), .Q(t_ff_1_q[2]), .reset(and_4_out));  // open: Qn, preset
  T_Flip_Flop #(.trigger("falling")) t_ff_10 (
    .T(1'b1), .clk(t_ff_3_q[1]), .Q(t_ff_3_q[2]), .reset(or_2_out));  // open: Qn, preset
  T_Flip_Flop #(.trigger("falling")) t_ff_11 (
    .T(1'b1), .clk(t_ff_4_q[1]), .Q(t_ff_4_q[2]), .reset(and_3_out));  // open: Qn, preset
  T_Flip_Flop #(.trigger("falling")) t_ff_12 (
    .T(1'b1), .clk(t_ff_1_q[2]), .Q(t_ff_1_q[3]), .reset(and_4_out));  // open: Qn, preset
  T_Flip_Flop #(.trigger("falling")) t_ff_13 (
    .T(1'b1), .clk(t_ff_3_q[2]), .Q(t_ff_3_q[3]), .reset(or_2_out));  // open: Qn, preset
  or or_1 (or_1_out, and_1_out, and_2_out);
  or or_2 (or_2_out, and_2_out, and_5_out);
  Hex_Digit_Display hex_digit_display_1 (.value({2'b00, t_ff_2_q}));  // open: dp
  Hex_Digit_Display hex_digit_display_2 (.value(t_ff_3_q));  // open: dp
  and and_1 (and_1_out, t_ff_2_q[1], t_ff_2_q[0]);
  and and_2 (and_2_out, t_ff_2_q[1], t_ff_3_q[2]);
  and and_3 (and_3_out, t_ff_4_q[0], t_ff_4_q[2]);
  and and_4 (and_4_out, t_ff_1_q[1], t_ff_1_q[3]);
  and and_5 (and_5_out, t_ff_3_q[1], t_ff_3_q[3]);
  Hex_Digit_Display hex_digit_display_3 (.value({1'b0, t_ff_4_q}));  // open: dp
  Hex_Digit_Display hex_digit_display_4 (.value(t_ff_1_q));  // open: dp
endmodule
