// Logisim project Informa_se_for_2_4_ou_10.circ as structural Verilog: 1 circuit, main circuit main
module main (
  input  A1,
  input  A3,
  input  A0,
  input  A2,
  output out_5
);

  wire or_1_out;

  or or_1 (or_1_out, A1, A3);
  and and_1 (out_5, or_1_out, ~A0, ~A2);  // AND_Gate
endmodule
