// Logisim project circuito_basico.circ as structural Verilog: 1 circuit, main circuit main
module main (
  input  A,
  input  B,
  output S1,
  output S2,
  output S3,
  output S4,
  output S5,
  output S6,
  output S7,
  output S8,
  output S9,
  output S10
);

  and Porta1 (S1, A, B);
  and and_1 (S2, ~A, B);  // AND_Gate
  and and_2 (S3, A, ~B);  // AND_Gate
  and and_3 (S4, ~A, ~B);  // AND_Gate
  nand nand_1 (S5, A, B);
  nor nor_1 (S6, A, B);
  or or_1 (S7, A, B);
  or or_2 (S8, ~A, B);  // OR_Gate
  or or_3 (S9, A, ~B);  // OR_Gate
  or or_4 (S10, ~A, ~B);  // OR_Gate
endmodule
